// Logisim project myex.circ as structural Verilog: 1 circuit, main circuit main
module main (
  input  in_1,
  output out_2,
  output [15:0] out_3,
  output [3:0] out_4
);

  assign out_3 = {{8{1'b0}}, {8{1'b1}}};  // Bit_Extender bit_extender_1
  Bit_Extender #(.out_width(4), .\type ("zero")) bit_extender_2 (.in({8{1'b1}}), .out(out_4));

  assign out_2 = in_1;

  // Other names for the same wires on the sheet: HI = in_1
endmodule
