// Logisim project ex2.circ as structural Verilog: 1 circuit, main circuit compute_BrUn
module compute_BrUn (
  input  [31:0] INSTRUCTION,
  output BrUn
);

  wire comparator_1_eq, comparator_2_eq;

  Comparator #(.mode("unsigned"), .width(7)) comparator_1 (
    .a(7'b1100011), .b(INSTRUCTION[6:0]), .eq(comparator_1_eq));  // open: gt, lt
  Comparator #(.mode("unsigned"), .width(2)) comparator_2 (
    .a(INSTRUCTION[14:13]), .b(2'b11), .eq(comparator_2_eq));  // open: gt, lt
  and and_1 (BrUn, comparator_1_eq, comparator_2_eq);
endmodule
