// Logisim project ex3.circ as structural Verilog: 1 circuit, main circuit non_pipelined
module non_pipelined (
  input  [7:0] in1,
  input  [7:0] in2,
  input  CLK,
  output [7:0] out1
);

  wire [7:0] adder_1_out, multiplier_1_out;

  Multiplier multiplier_1 (.a(in1), .b(in2), .out(multiplier_1_out));  // open: cin, cout
  Adder adder_1 (.a(multiplier_1_out), .b(out1), .out(adder_1_out));  // open: cin, cout
  Register register_1 (.D(adder_1_out), .clk(CLK), .Q(out1));  // open: en, clr

  // Notes on the sheet:
  //   125
endmodule
